// Logisim project 4BitCPU.circ as structural Verilog: 5 circuits, main circuit main
module main (
);

  wire clock_1_out, cpu_1_out_en, cpu_1_wr_en, HLT, RESET_out, Z_FLAG;
  wire [1:0] STATE_REG;
  wire [3:0] cpu_1_acc_out, cpu_1_d, cpu_1_pr_out;
  wire [7:0] cpu_1_addr, cpu_1_d_in, MAR_REG, PC_REG, ram_1_dout;

  Clock clock_1 (.out(clock_1_out));
  Button RESET (.out(RESET_out));
  // LedBar #(.inputtype("row")) ledbar_1: pin names not known; wires that end beside it: MAR_REG
  // LedBar #(.inputtype("row")) ledbar_2: pin names not known; wires that end beside it: PC_REG
  // LedBar #(.inputtype("row"), .matrixcols(2)) ledbar_3: pin names not known; wires that end beside it: STATE_REG
  // LedBar #(.inputtype("row"), .matrixcols(1)) ledbar_4: pin names not known; wires that end beside it: Z_FLAG
  // LedBar #(.inputtype("row"), .matrixcols(1)) ledbar_5: pin names not known; wires that end beside it: HLT
  RAM ram_1 (
    .addr(cpu_1_addr), .we(cpu_1_wr_en), .oe(cpu_1_out_en), .clk(clock_1_out), .din(cpu_1_d_in),
    .dout(ram_1_dout));
  CPU cpu_1 (
    .RST(RESET_out), .D_OUT(ram_1_dout), .CLK(clock_1_out), .D(cpu_1_d), .ACC_OUT(cpu_1_acc_out),
    .PR_OUT(cpu_1_pr_out), .STATE_OUT(STATE_REG), .Z_FLAG_OUT(Z_FLAG), .MAR_OUT(MAR_REG), .D_IN(cpu_1_d_in),
    .ADDR(cpu_1_addr), .WR_EN(cpu_1_wr_en), .OUT_EN(cpu_1_out_en), .PC_OUT(PC_REG), .HLT(HLT));
  Hex_Digit_Display hex_digit_display_1 (.value(cpu_1_acc_out));  // open: dp
  Hex_Digit_Display hex_digit_display_2 (.value(cpu_1_d));  // open: dp
  Hex_Digit_Display hex_digit_display_3 (.value(cpu_1_pr_out));  // open: dp

  // Notes on the sheet:
  //   Accumulator
  //   Data
  //   Page Register
endmodule

module cpu_standalone (
  input  in_1
);

  wire ACC_SEL, alu_1_zero_flag, and_2_out, CLK, clock_1_out, d_ff_1_q, d_ff_1_qn, d_ff_2_q, HLT, IMD,
       LD_ADD, LD_MEM, not_1_out, not_2_out, or_1_out, or_2_out, PC_INC, RST_STATE, UNARY, WR_ACC, WR_IR,
       WR_MEM, WR_PC, WR_PR, WR_ZF, ZERO_FLAG_q;
  wire [1:0] STATE_q;
  wire [2:0] ALU_SEL;
  wire [3:0] ACC_OUT, alu_1_data, IR_q, multiplexer_2_out;
  wire [7:0] MAR, MAR_q, multiplexer_1_out, ram_1_dout;
  wire [7:4] ram_1_dout_2;

  Counter u_MAR (.clr(in_1), .load(LD_ADD), .count(1'b0), .clk(CLK), .D(MAR), .Q(MAR_q));  // open: up, carry
  or or_1 (or_1_out, RST_STATE, PC_INC);
  Multiplexer #(.width(8)) multiplexer_1 (.in0(MAR_q), .in1(ram_1_dout), .out(multiplexer_1_out), .sel(IMD));
  RAM ram_1 (
    .addr(multiplexer_1_out), .we(WR_MEM), .oe(LD_MEM), .clk(CLK), .din({4'b0000, ACC_OUT}),
    .dout({ram_1_dout_2, ram_1_dout[3:0]}));
  Counter PC (.clr(in_1), .load(WR_PC), .clk(or_1_out), .D(ram_1_dout), .Q(MAR));  // open: up, count, carry
  Clock clock_1 (.out(clock_1_out));
  not not_1 (not_1_out, HLT);
  Multiplexer #(.width(4)) multiplexer_2 (
    .in0(ram_1_dout[3:0]), .in1(alu_1_data), .out(multiplexer_2_out), .sel(ACC_SEL));
  // LedBar #(.inputtype("row"), .matrixcols(3)) ledbar_1: pin names not known; wires that end beside it: ALU_SEL
  and and_1 (CLK, not_1_out, clock_1_out);
  Register #(.trigger("falling"), .width(4)) IR (.D(ram_1_dout_2), .en(WR_IR), .clk(CLK), .Q(IR_q), .clr(in_1));
  Register #(.width(4)) ACC (.D(multiplexer_2_out), .en(WR_ACC), .clk(CLK), .Q(ACC_OUT), .clr(in_1));
  Register #(.width(4)) PR (.D(ram_1_dout[3:0]), .en(WR_PR), .clk(CLK), .Q(ram_1_dout[7:4]), .clr(in_1));
  Counter #(.max('h3), .trigger("falling"), .width(2)) STATE (
    .clr(or_2_out), .clk(CLK), .carry(PC_INC), .Q(STATE_q));  // open: load, up, count, D
  D_Flip_Flop d_ff_1 (.D(d_ff_1_qn), .clk(RST_STATE), .Q(d_ff_1_q), .Qn(d_ff_1_qn));  // open: preset, reset
  D_Flip_Flop d_ff_2 (.D(RST_STATE), .clk(CLK), .Q(d_ff_2_q));  // open: Qn, preset, reset
  not not_2 (not_2_out, RST_STATE);
  and and_2 (and_2_out, not_2_out, d_ff_2_q);
  ALU alu_1 (
    .ACC(ACC_OUT), .MDR(ram_1_dout[3:0]), .UNARY(UNARY), .SEL(ALU_SEL), .DATA(alu_1_data),
    .ZERO_FLAG(alu_1_zero_flag));
  or or_2 (or_2_out, and_2_out, in_1);
  Register #(.width(1)) ZERO_FLAG (.D(alu_1_zero_flag), .en(WR_ZF), .clk(CLK), .Q(ZERO_FLAG_q), .clr(in_1));
  CU_LOGIC cu_logic_1 (
    .Z_FLAG(ZERO_FLAG_q), .STATE(STATE_q), .IR(IR_q), .WR_IR(WR_IR), .WR_ACC(WR_ACC), .WR_PR(WR_PR),
    .WR_ZF(WR_ZF), .WR_PC(WR_PC), .IMD(IMD), .ALU_SEL(ALU_SEL), .ACC_SEL(ACC_SEL), .UNARY(UNARY),
    .LD_ADD(LD_ADD), .WR_MEM(WR_MEM), .LD_MEM(LD_MEM), .RST_STATE(RST_STATE), .HLT(HLT));

  // Other names for the same wires on the sheet: RST = in_1
endmodule

module ALU (
  input  [3:0] ACC,
  input  [3:0] MDR,
  input  UNARY,
  input  [2:0] SEL,
  output [3:0] DATA,
  output ZERO_FLAG
);

  wire [3:0] adder_1_out, and_1_out, multiplexer_1_out, or_1_out, subtractor_1_out, xor_1_out;

  Multiplexer #(.width(4)) multiplexer_1 (.in0(MDR), .in1(4'b0001), .out(multiplexer_1_out), .sel(UNARY));
  Adder #(.width(4)) adder_1 (.a(ACC), .b(multiplexer_1_out), .out(adder_1_out));  // open: cin, cout
  Subtractor #(.width(4)) subtractor_1 (.a(ACC), .b(multiplexer_1_out), .out(subtractor_1_out));  // open: bin, bout
  assign and_1_out = ACC & MDR;  // AND_Gate and_1, 4 bits wide
  assign or_1_out = ACC | MDR;  // OR_Gate or_1, 4 bits wide
  assign xor_1_out = ACC ^ MDR;  // XOR_Gate xor_1, 4 bits wide
  Multiplexer #(.select(3), .width(4)) multiplexer_2 (
    .in0(adder_1_out), .in1(subtractor_1_out), .in2(and_1_out), .in3(or_1_out), .in4(xor_1_out), .out(DATA),
    .sel(SEL));  // open: in5, in6, in7
  nor nor_1 (ZERO_FLAG, DATA[0], DATA[1], DATA[2], DATA[3]);
endmodule

module CU_LOGIC (
  input  Z_FLAG,
  input  [1:0] STATE,
  input  [3:0] IR,
  output WR_IR,
  output WR_ACC,
  output WR_PR,
  output WR_ZF,
  output WR_PC,
  output IMD,
  output [2:0] ALU_SEL,
  output ACC_SEL,
  output UNARY,
  output LD_ADD,
  output WR_MEM,
  output LD_MEM,
  output RST_STATE,
  output HLT
);

  wire and_2_out, and_3_out, and_4_out, and_5_out, and_6_out, and_7_out, and_8_out, and_9_out, and_10_out,
       and_11_out, and_12_out, and_13_out, and_14_out, and_15_out, and_16_out, and_17_out, and_18_out,
       and_19_out, and_20_out, and_21_out, and_22_out, and_23_out, and_24_out, and_25_out, and_26_out,
       and_27_out, and_28_out, and_29_out, and_30_out, and_31_out, and_32_out, and_33_out, and_34_out,
       and_35_out, and_36_out, and_37_out, and_38_out, and_39_out, and_40_out, and_41_out, and_42_out,
       and_43_out, and_44_out, and_45_out, and_46_out, and_47_out, and_48_out, and_49_out, and_50_out,
       and_51_out, and_52_out, and_53_out, and_54_out, and_55_out, and_56_out, and_57_out, and_58_out,
       and_59_out, and_60_out, and_61_out, and_62_out, and_63_out, and_64_out, and_65_out, and_66_out,
       and_67_out, and_68_out, and_69_out, and_70_out, and_71_out, and_72_out, and_73_out, and_74_out,
       and_75_out, and_76_out, and_77_out, and_78_out, and_79_out, and_80_out, and_81_out, and_82_out,
       and_83_out, and_84_out, and_85_out, and_86_out, and_87_out, and_88_out, and_89_out, and_90_out,
       and_91_out, and_92_out, and_93_out, and_94_out, and_95_out, and_96_out, and_97_out, and_98_out,
       and_99_out, and_100_out, and_101_out, and_102_out, and_103_out, and_104_out, and_105_out, and_106_out,
       and_107_out, and_108_out, and_109_out, and_110_out, and_111_out, and_112_out, and_113_out,
       and_114_out, and_115_out, and_116_out, and_117_out, and_118_out, and_119_out, and_120_out,
       and_121_out, and_122_out, and_123_out, and_124_out, and_125_out, and_126_out, and_127_out,
       and_128_out, and_129_out, and_130_out, and_131_out, and_132_out, and_133_out, and_134_out,
       and_135_out, and_136_out, and_137_out, and_138_out, and_139_out, and_140_out, and_141_out,
       and_142_out, and_143_out, and_144_out, and_145_out, and_146_out, and_147_out, and_148_out,
       and_149_out, and_150_out, and_151_out, and_152_out, and_153_out, and_154_out, and_155_out,
       and_156_out, and_157_out, and_158_out, and_159_out, and_160_out, and_161_out, and_162_out,
       and_163_out, and_164_out, and_165_out, and_166_out, and_167_out, and_168_out, and_169_out,
       and_170_out, and_171_out, and_172_out, and_173_out, and_174_out, and_176_out, and_177_out,
       and_178_out, and_179_out, and_180_out, and_181_out, and_182_out, and_183_out, and_185_out,
       and_186_out, and_187_out, and_188_out, and_189_out, and_190_out, and_191_out, and_192_out,
       and_193_out, and_194_out, and_195_out, and_196_out, and_197_out, and_198_out, and_199_out,
       and_200_out, and_201_out, and_202_out, and_203_out, and_204_out, and_205_out, and_206_out,
       and_207_out, and_208_out, and_209_out, and_210_out, and_211_out, and_212_out, and_213_out,
       and_214_out, and_215_out, and_216_out, and_217_out, and_218_out, and_219_out, and_220_out,
       and_221_out, and_222_out, and_223_out, and_224_out, and_225_out, and_226_out, and_227_out,
       and_228_out, and_229_out, and_230_out, and_232_out, and_233_out, and_234_out, and_235_out,
       and_236_out, and_237_out, and_238_out, and_239_out, and_240_out, and_241_out, and_242_out,
       and_243_out, and_244_out, and_245_out, and_246_out, and_247_out, and_248_out, and_249_out,
       and_250_out, and_251_out, not_1_out, not_2_out, not_3_out, not_4_out, not_5_out, not_6_out, not_7_out,
       or_1_out, or_2_out, or_3_out, or_4_out, or_5_out, or_6_out, or_9_out, or_10_out, or_11_out, or_12_out,
       or_13_out, or_14_out, or_15_out, or_16_out, or_17_out, or_18_out, or_19_out, or_21_out, or_22_out,
       or_23_out, or_24_out, or_26_out, or_31_out, or_33_out, or_35_out, or_36_out, or_37_out, or_38_out,
       or_39_out, or_40_out, or_41_out, or_43_out;

  not not_1 (not_1_out, Z_FLAG);
  not not_2 (not_2_out, STATE[1]);
  not not_3 (not_3_out, STATE[0]);
  not not_4 (not_4_out, IR[3]);
  not not_5 (not_5_out, IR[2]);
  not not_6 (not_6_out, IR[1]);
  not not_7 (not_7_out, IR[0]);
  and and_1 (WR_IR, not_2_out, not_3_out);
  and and_2 (and_2_out, STATE[1], not_3_out);
  and and_3 (and_3_out, STATE[1], not_3_out);
  and and_4 (and_4_out, STATE[1], not_3_out);
  and and_5 (and_5_out, not_2_out, STATE[0]);
  and and_6 (and_6_out, IR[2], not_6_out);
  and and_7 (and_7_out, STATE[1], not_3_out);
  and and_8 (and_8_out, not_5_out, not_6_out);
  and and_9 (and_9_out, STATE[1], not_3_out);
  and and_10 (and_10_out, STATE[1], not_3_out);
  and and_11 (and_11_out, not_2_out, STATE[0]);
  and and_12 (and_12_out, not_5_out, not_6_out);
  and and_13 (and_13_out, not_1_out, not_2_out);
  and and_14 (and_14_out, STATE[0], IR[3]);
  and and_15 (and_15_out, not_5_out, IR[1]);
  and and_16 (and_16_out, not_2_out, STATE[0]);
  and and_17 (and_17_out, not_5_out, not_6_out);
  and and_18 (and_18_out, not_2_out, STATE[0]);
  and and_19 (and_19_out, not_5_out, IR[1]);
  and and_20 (and_20_out, not_2_out, STATE[0]);
  and and_21 (and_21_out, not_5_out, not_6_out);
  and and_22 (and_22_out, STATE[1], not_3_out);
  and and_23 (and_23_out, not_5_out, not_6_out);
  and and_24 (and_24_out, not_2_out, STATE[0]);
  and and_25 (and_25_out, STATE[1], not_3_out);
  and and_26 (and_26_out, not_2_out, STATE[0]);
  and and_27 (and_27_out, STATE[1], not_3_out);
  and and_28 (and_28_out, not_2_out, STATE[0]);
  and and_29 (and_29_out, IR[2], IR[1]);
  and and_30 (and_30_out, STATE[1], not_3_out);
  and and_31 (and_31_out, IR[2], IR[1]);
  and and_32 (and_32_out, not_2_out, STATE[0]);
  and and_33 (and_33_out, not_5_out, not_6_out);
  and and_34 (and_34_out, not_2_out, STATE[0]);
  and and_35 (and_35_out, not_2_out, STATE[0]);
  and and_36 (and_36_out, STATE[1], not_3_out);
  and and_37 (and_37_out, not_5_out, not_6_out);
  and and_38 (and_38_out, STATE[1], not_3_out);
  and and_39 (and_39_out, STATE[1], not_3_out);
  and and_40 (and_40_out, not_2_out, STATE[0]);
  and and_41 (and_41_out, IR[2], not_6_out);
  and and_42 (and_42_out, STATE[1], not_3_out);
  and and_43 (and_43_out, IR[2], not_6_out);
  and and_44 (and_44_out, not_2_out, STATE[0]);
  and and_45 (and_45_out, IR[2], IR[1]);
  and and_46 (and_46_out, STATE[1], not_3_out);
  and and_47 (and_47_out, IR[2], IR[1]);
  and and_48 (and_48_out, STATE[1], IR[3]);
  and and_49 (and_49_out, Z_FLAG, STATE[1]);
  and and_50 (and_50_out, not_5_out, IR[1]);
  and and_51 (and_51_out, STATE[1], IR[3]);
  and and_52 (and_52_out, STATE[1], not_3_out);
  and and_53 (and_53_out, not_5_out, IR[1]);
  and and_54 (and_54_out, not_2_out, not_4_out);
  and and_55 (and_55_out, STATE[1], not_3_out);
  and and_56 (and_56_out, not_5_out, IR[1]);
  and and_57 (and_57_out, not_1_out, STATE[1]);
  and and_58 (and_58_out, not_3_out, IR[3]);
  and and_59 (and_59_out, not_5_out, IR[1]);
  and and_60 (and_60_out, STATE[1], not_3_out);
  and and_61 (and_61_out, IR[2], not_6_out);
  and and_62 (and_62_out, STATE[1], not_3_out);
  and and_63 (and_63_out, IR[2], IR[1]);
  and and_64 (and_64_out, not_2_out, STATE[0]);
  and and_65 (and_65_out, not_2_out, STATE[0]);
  and and_66 (and_66_out, IR[3], IR[2]);
  and and_67 (and_67_out, IR[1], IR[0]);
  and and_68 (and_68_out, and_2_out, not_4_out);
  and and_69 (and_69_out, not_6_out, IR[0]);
  and and_70 (and_70_out, STATE[1], not_3_out);
  and and_71 (and_71_out, not_4_out, IR[2]);
  and and_72 (and_72_out, STATE[1], not_3_out);
  and and_73 (and_73_out, not_5_out, not_6_out);
  and and_74 (and_74_out, and_3_out, IR[2]);
  and and_75 (and_75_out, not_6_out, IR[0]);
  and and_76 (and_76_out, and_4_out, IR[2]);
  and and_77 (and_77_out, IR[1], not_7_out);
  and and_78 (and_78_out, not_2_out, STATE[0]);
  and and_79 (and_79_out, not_5_out, IR[1]);
  and and_80 (and_80_out, and_5_out, IR[3]);
  and and_81 (and_81_out, and_6_out, not_7_out);
  and and_82 (and_82_out, STATE[1], not_3_out);
  and and_83 (and_83_out, not_4_out, IR[2]);
  and and_84 (and_84_out, and_7_out, IR[3]);
  and and_85 (and_85_out, and_8_out, not_7_out);
  and and_86 (and_86_out, and_9_out, IR[2]);
  and and_87 (and_87_out, not_6_out, IR[0]);
  and and_88 (and_88_out, and_10_out, IR[2]);
  and and_89 (and_89_out, IR[1], not_7_out);
  and and_90 (and_90_out, and_11_out, IR[3]);
  and and_91 (and_91_out, and_12_out, IR[0]);
  and and_92 (and_92_out, and_13_out, and_14_out);
  and and_93 (and_93_out, and_15_out, not_7_out);
  and and_94 (and_94_out, Z_FLAG, not_2_out);
  and and_95 (and_95_out, IR[3], not_5_out);
  and and_96 (and_96_out, and_16_out, not_4_out);
  and and_97 (and_97_out, and_17_out, IR[0]);
  and and_98 (and_98_out, and_18_out, not_4_out);
  and and_99 (and_99_out, and_19_out, not_7_out);
  and and_100 (and_100_out, STATE[1], not_3_out);
  and and_101 (and_101_out, not_5_out, IR[1]);
  and and_102 (and_102_out, and_20_out, IR[3]);
  and and_103 (and_103_out, and_21_out, not_7_out);
  and and_104 (and_104_out, and_22_out, IR[3]);
  and and_105 (and_105_out, and_23_out, not_7_out);
  and and_106 (and_106_out, and_24_out, not_4_out);
  and and_107 (and_107_out, IR[2], IR[1]);
  and and_108 (and_108_out, and_25_out, not_4_out);
  and and_109 (and_109_out, IR[2], IR[1]);
  and and_110 (and_110_out, and_26_out, not_4_out);
  and and_111 (and_111_out, IR[2], IR[0]);
  and and_112 (and_112_out, and_27_out, not_4_out);
  and and_113 (and_113_out, IR[2], IR[0]);
  and and_114 (and_114_out, and_28_out, IR[3]);
  and and_115 (and_115_out, and_29_out, not_7_out);
  and and_116 (and_116_out, and_30_out, IR[3]);
  and and_117 (and_117_out, and_31_out, not_7_out);
  and and_118 (and_118_out, not_2_out, STATE[0]);
  and and_119 (and_119_out, not_4_out, IR[2]);
  and and_120 (and_120_out, and_32_out, IR[3]);
  and and_121 (and_121_out, and_33_out, not_7_out);
  and and_122 (and_122_out, and_34_out, IR[2]);
  and and_123 (and_123_out, not_6_out, IR[0]);
  and and_124 (and_124_out, and_35_out, IR[2]);
  and and_125 (and_125_out, IR[1], not_7_out);
  and and_126 (and_126_out, STATE[1], not_3_out);
  and and_127 (and_127_out, not_4_out, IR[2]);
  and and_128 (and_128_out, and_36_out, IR[3]);
  and and_129 (and_129_out, and_37_out, not_7_out);
  and and_130 (and_130_out, and_38_out, IR[2]);
  and and_131 (and_131_out, not_6_out, IR[0]);
  and and_132 (and_132_out, and_39_out, IR[2]);
  and and_133 (and_133_out, IR[1], not_7_out);
  and and_134 (and_134_out, and_40_out, IR[3]);
  and and_135 (and_135_out, and_41_out, IR[0]);
  and and_136 (and_136_out, and_42_out, IR[3]);
  and and_137 (and_137_out, and_43_out, IR[0]);
  and and_138 (and_138_out, and_44_out, IR[3]);
  and and_139 (and_139_out, and_45_out, not_7_out);
  and and_140 (and_140_out, and_46_out, IR[3]);
  and and_141 (and_141_out, and_47_out, not_7_out);
  and and_142 (and_142_out, STATE[0], IR[3]);
  and and_143 (and_143_out, not_5_out, IR[0]);
  and and_144 (and_144_out, STATE[0], IR[3]);
  and and_145 (and_145_out, not_5_out, IR[1]);
  and and_146 (and_146_out, STATE[1], not_3_out);
  and and_147 (and_147_out, not_5_out, IR[1]);
  and and_148 (and_148_out, and_48_out, not_5_out);
  and and_149 (and_149_out, not_6_out, IR[0]);
  and and_150 (and_150_out, and_49_out, IR[3]);
  and and_151 (and_151_out, and_50_out, not_7_out);
  and and_152 (and_152_out, STATE[1], IR[3]);
  and and_153 (and_153_out, and_51_out, IR[2]);
  and and_154 (and_154_out, IR[1], IR[0]);
  and and_155 (and_155_out, STATE[1], STATE[0]);
  and and_156 (and_156_out, not_1_out, STATE[1]);
  and and_157 (and_157_out, and_52_out, not_4_out);
  and and_158 (and_158_out, and_53_out, not_7_out);
  and and_159 (and_159_out, and_54_out, not_5_out);
  and and_160 (and_160_out, not_6_out, IR[0]);
  and and_161 (and_161_out, and_55_out, not_4_out);
  and and_162 (and_162_out, and_56_out, IR[0]);
  and and_163 (and_163_out, and_57_out, and_58_out);
  and and_164 (and_164_out, and_59_out, not_7_out);
  and and_165 (and_165_out, and_60_out, IR[3]);
  and and_166 (and_166_out, and_61_out, not_7_out);
  and and_167 (and_167_out, and_62_out, IR[3]);
  and and_168 (and_168_out, and_63_out, IR[0]);
  and and_169 (and_169_out, and_64_out, IR[3]);
  and and_170 (and_170_out, not_5_out, IR[0]);
  and and_171 (and_171_out, and_65_out, IR[3]);
  and and_172 (and_172_out, not_5_out, IR[1]);
  and and_173 (and_173_out, Z_FLAG, STATE[1]);
  and and_174 (and_174_out, not_5_out, IR[1]);
  and and_175 (HLT, and_66_out, and_67_out);
  and and_176 (and_176_out, and_68_out, and_69_out);
  and and_177 (and_177_out, and_70_out, and_71_out);
  and and_178 (and_178_out, and_72_out, IR[3]);
  and and_179 (and_179_out, and_73_out, not_7_out);
  and and_180 (and_180_out, and_74_out, and_75_out);
  and and_181 (and_181_out, and_76_out, and_77_out);
  and and_182 (and_182_out, and_78_out, not_4_out);
  and and_183 (and_183_out, and_79_out, IR[0]);
  and and_184 (WR_PR, and_80_out, and_81_out);
  and and_185 (and_185_out, and_82_out, and_83_out);
  and and_186 (and_186_out, and_84_out, and_85_out);
  and and_187 (and_187_out, and_86_out, and_87_out);
  and and_188 (and_188_out, and_88_out, and_89_out);
  and and_189 (and_189_out, and_90_out, and_91_out);
  and and_190 (and_190_out, and_92_out, and_93_out);
  and and_191 (and_191_out, and_94_out, STATE[0]);
  and and_192 (and_192_out, and_95_out, IR[0]);
  and and_193 (and_193_out, and_96_out, and_97_out);
  and and_194 (and_194_out, and_98_out, and_99_out);
  and and_195 (and_195_out, and_100_out, not_4_out);
  and and_196 (and_196_out, and_101_out, not_7_out);
  and and_197 (and_197_out, and_102_out, and_103_out);
  and and_198 (and_198_out, and_104_out, and_105_out);
  and and_199 (and_199_out, and_106_out, and_107_out);
  and and_200 (and_200_out, and_108_out, and_109_out);
  and and_201 (and_201_out, and_110_out, and_111_out);
  and and_202 (and_202_out, and_112_out, and_113_out);
  and and_203 (and_203_out, and_114_out, and_115_out);
  and and_204 (and_204_out, and_116_out, and_117_out);
  and and_205 (and_205_out, and_118_out, and_119_out);
  and and_206 (and_206_out, and_120_out, and_121_out);
  and and_207 (and_207_out, and_122_out, and_123_out);
  and and_208 (and_208_out, and_124_out, and_125_out);
  and and_209 (and_209_out, and_126_out, and_127_out);
  and and_210 (and_210_out, and_128_out, and_129_out);
  and and_211 (and_211_out, and_130_out, and_131_out);
  and and_212 (and_212_out, and_132_out, and_133_out);
  and and_213 (and_213_out, and_134_out, and_135_out);
  and and_214 (and_214_out, and_136_out, and_137_out);
  and and_215 (and_215_out, and_138_out, and_139_out);
  and and_216 (and_216_out, and_140_out, and_141_out);
  and and_217 (and_217_out, and_142_out, and_143_out);
  and and_218 (and_218_out, and_144_out, and_145_out);
  and and_219 (and_219_out, and_146_out, not_4_out);
  and and_220 (and_220_out, and_147_out, IR[0]);
  and and_221 (and_221_out, and_148_out, and_149_out);
  and and_222 (and_222_out, and_150_out, and_151_out);
  and and_223 (and_223_out, and_152_out, IR[2]);
  and and_224 (and_224_out, not_6_out, not_7_out);
  and and_225 (and_225_out, and_153_out, and_154_out);
  and and_226 (and_226_out, and_155_out, not_6_out);
  and and_227 (and_227_out, STATE[1], STATE[0]);
  and and_228 (and_228_out, STATE[1], STATE[0]);
  and and_229 (and_229_out, and_156_out, IR[3]);
  and and_230 (and_230_out, not_5_out, IR[0]);
  and and_231 (WR_MEM, and_157_out, and_158_out);
  and and_232 (and_232_out, not_2_out, not_3_out);
  and and_233 (and_233_out, and_159_out, and_160_out);
  and and_234 (and_234_out, and_161_out, and_162_out);
  and and_235 (and_235_out, and_163_out, and_164_out);
  and and_236 (and_236_out, and_165_out, and_166_out);
  and and_237 (and_237_out, and_167_out, and_168_out);
  and and_238 (and_238_out, and_169_out, and_170_out);
  and and_239 (and_239_out, and_171_out, and_172_out);
  and and_240 (and_240_out, and_173_out, not_3_out);
  and and_241 (and_241_out, and_174_out, IR[0]);
  or or_1 (or_1_out, and_176_out, and_177_out);
  and and_242 (and_242_out, and_178_out, and_179_out);
  or or_2 (or_2_out, and_180_out, and_181_out);
  and and_243 (and_243_out, and_182_out, and_183_out);
  or or_3 (or_3_out, and_185_out, and_186_out);
  or or_4 (or_4_out, and_187_out, and_188_out);
  or or_5 (or_5_out, and_189_out, and_190_out);
  and and_244 (and_244_out, and_191_out, and_192_out);
  or or_6 (or_6_out, and_193_out, and_194_out);
  and and_245 (and_245_out, and_195_out, and_196_out);
  or or_7 (ALU_SEL[2], and_197_out, and_198_out);
  or or_8 (ALU_SEL[1], and_199_out, and_200_out);
  or or_9 (or_9_out, and_201_out, and_202_out);
  or or_10 (or_10_out, and_203_out, and_204_out);
  or or_11 (or_11_out, and_205_out, and_206_out);
  or or_12 (or_12_out, and_207_out, and_208_out);
  or or_13 (or_13_out, and_209_out, and_210_out);
  or or_14 (or_14_out, and_211_out, and_212_out);
  or or_15 (or_15_out, and_213_out, and_214_out);
  or or_16 (or_16_out, and_215_out, and_216_out);
  or or_17 (or_17_out, and_217_out, and_218_out);
  and and_246 (and_246_out, and_219_out, and_220_out);
  or or_18 (or_18_out, and_221_out, and_222_out);
  and and_247 (and_247_out, and_223_out, and_224_out);
  or or_19 (or_19_out, and_225_out, and_226_out);
  and and_248 (and_248_out, and_227_out, not_7_out);
  and and_249 (and_249_out, and_228_out, IR[2]);
  and and_250 (and_250_out, and_229_out, and_230_out);
  or or_20 (LD_MEM, and_232_out, and_233_out);
  or or_21 (or_21_out, and_234_out, and_235_out);
  or or_22 (or_22_out, and_236_out, and_237_out);
  or or_23 (or_23_out, and_238_out, and_239_out);
  and and_251 (and_251_out, and_240_out, and_241_out);
  or or_24 (or_24_out, or_1_out, and_242_out);
  or or_25 (WR_ACC, or_24_out, or_26_out);
  or or_26 (or_26_out, or_2_out, and_243_out);
  or or_27 (WR_ZF, or_3_out, or_4_out);
  or or_28 (WR_PC, or_5_out, and_244_out);
  or or_29 (IMD, or_6_out, and_245_out);
  or or_30 (ALU_SEL[0], or_9_out, or_10_out);
  or or_31 (or_31_out, or_11_out, or_12_out);
  or or_32 (ACC_SEL, or_31_out, or_33_out);
  or or_33 (or_33_out, or_13_out, or_14_out);
  or or_34 (UNARY, or_15_out, or_16_out);
  or or_35 (or_35_out, or_17_out, and_246_out);
  or or_36 (or_36_out, or_35_out, or_37_out);
  or or_37 (or_37_out, or_18_out, and_247_out);
  or or_38 (or_38_out, or_19_out, and_248_out);
  or or_39 (or_39_out, or_38_out, or_40_out);
  or or_40 (or_40_out, and_249_out, and_250_out);
  or or_41 (or_41_out, or_21_out, or_22_out);
  or or_42 (RST_STATE, or_41_out, or_43_out);
  or or_43 (or_43_out, or_23_out, and_251_out);
  or or_44 (LD_ADD, or_36_out, or_39_out);
endmodule

module CPU (
  input  RST,
  input  CLK,
  input  [7:0] D_OUT,
  output HLT,
  output [1:0] STATE_OUT,
  output [7:0] MAR_OUT,
  output [7:0] ADDR,
  output WR_EN,
  output OUT_EN,
  output [3:0] ACC_OUT,
  output [7:0] D_IN,
  output [3:0] PR_OUT,
  output Z_FLAG_OUT,
  output [3:0] D,
  output [7:0] PC_OUT
);

  wire ACC_SEL, alu_1_zero_flag, and_2_out, CLK_t, d_ff_1_q, IMD, LD_ADD, not_1_out, not_2_out, or_1_out,
       or_2_out, PC_INC, RST_STATE, UNARY, WR_ACC, WR_IR, WR_PC, WR_PR, WR_ZF;
  wire [2:0] ALU_SEL;
  wire [3:0] alu_1_data, IR_q, multiplexer_2_out;

  Counter MAR (.clr(RST), .load(LD_ADD), .count(1'b0), .clk(CLK_t), .D(PC_OUT), .Q(MAR_OUT));  // open: up, carry
  or or_1 (or_1_out, RST_STATE, PC_INC);
  Multiplexer #(.width(8)) multiplexer_1 (.in0(MAR_OUT), .in1({PR_OUT, D_OUT[3:0]}), .out(ADDR), .sel(IMD));
  Counter PC (.clr(RST), .load(WR_PC), .clk(or_1_out), .D({PR_OUT, D_OUT[3:0]}), .Q(PC_OUT));  // open: up, count, carry
  not not_1 (not_1_out, HLT);
  Multiplexer #(.width(4)) multiplexer_2 (.in0(D_OUT[3:0]), .in1(alu_1_data), .out(multiplexer_2_out), .sel(ACC_SEL));
  // LedBar #(.inputtype("row"), .matrixcols(3)) ledbar_1: pin names not known; wires that end beside it: ALU_SEL
  and and_1 (CLK_t, not_1_out, CLK);
  Register #(.trigger("falling"), .width(4)) IR (.D(D_OUT[7:4]), .en(WR_IR), .clk(CLK_t), .Q(IR_q), .clr(RST));
  Register #(.width(4)) ACC (.D(multiplexer_2_out), .en(WR_ACC), .clk(CLK_t), .Q(ACC_OUT), .clr(RST));
  Register #(.width(4)) PR (.D(D_OUT[3:0]), .en(WR_PR), .clk(CLK_t), .Q(PR_OUT), .clr(RST));
  Counter #(.max('h3), .trigger("falling"), .width(2)) STATE (
    .clr(or_2_out), .clk(CLK_t), .carry(PC_INC), .Q(STATE_OUT));  // open: load, up, count, D
  D_Flip_Flop d_ff_1 (.D(RST_STATE), .clk(CLK_t), .Q(d_ff_1_q));  // open: Qn, preset, reset
  not not_2 (not_2_out, RST_STATE);
  and and_2 (and_2_out, not_2_out, d_ff_1_q);
  ALU alu_1 (
    .ACC(ACC_OUT), .MDR(D_OUT[3:0]), .UNARY(UNARY), .SEL(ALU_SEL), .DATA(alu_1_data),
    .ZERO_FLAG(alu_1_zero_flag));
  or or_2 (or_2_out, and_2_out, RST);
  Register #(.width(1)) ZERO_FLAG (.D(alu_1_zero_flag), .en(WR_ZF), .clk(CLK_t), .Q(Z_FLAG_OUT), .clr(RST));
  CU_LOGIC cu_logic_1 (
    .Z_FLAG(Z_FLAG_OUT), .STATE(STATE_OUT), .IR(IR_q), .WR_IR(WR_IR), .WR_ACC(WR_ACC), .WR_PR(WR_PR),
    .WR_ZF(WR_ZF), .WR_PC(WR_PC), .IMD(IMD), .ALU_SEL(ALU_SEL), .ACC_SEL(ACC_SEL), .UNARY(UNARY),
    .LD_ADD(LD_ADD), .WR_MEM(WR_EN), .LD_MEM(OUT_EN), .RST_STATE(RST_STATE), .HLT(HLT));

  assign D = D_OUT[3:0];
  assign D_IN = {4'b0000, ACC_OUT};

  // Other names for the same wires on the sheet: LD_MEM = OUT_EN; MAR[7:0] = PC_OUT; WR_MEM = WR_EN
endmodule
